// Logisim project ETFStudent.circ as structural Verilog: 12 circuits, main circuit REG32_LD
module REG32_LD (
  input  [31:0] I15__0,
  input  LD,
  input  mr,
  input  CLK,
  output [31:0] A15__0
);

  // REG16_LD reg16_ld_1: pin names not known; wires that end beside it: CLK, mr, I15__0[31:16], A15__0[31:16], LD
  // REG16_LD reg16_ld_2: pin names not known; wires that end beside it: CLK, mr, I15__0[15:0], A15__0[15:0], LD

  // Notes on the sheet:
  //   __
endmodule

module KMADR (
  input  immed,
  input  memdir,
  input  regdir,
  input  regind,
  input  brpom,
  input  brxpom,
  output [4:0] Adr4__0
);

  assign Adr4__0 = immed ? 5'b00010 : 5'bz;  // Controlled_Buffer controlled_buffer_1
  assign Adr4__0 = memdir ? 5'b00100 : 5'bz;  // Controlled_Buffer controlled_buffer_2
  assign Adr4__0 = regdir ? 5'b01011 : 5'bz;  // Controlled_Buffer controlled_buffer_3
  assign Adr4__0 = regind ? 5'b01101 : 5'bz;  // Controlled_Buffer controlled_buffer_4
  assign Adr4__0 = brpom ? 5'b01110 : 5'bz;  // Controlled_Buffer controlled_buffer_5
  assign Adr4__0 = brxpom ? 5'b01111 : 5'bz;  // Controlled_Buffer controlled_buffer_6
endmodule

module KMOPR (
  input  HALT,
  input  RTI,
  input  RTS,
  input  INTE,
  input  INTD,
  input  PUSH,
  input  POP,
  input  STBR,
  input  STXR,
  input  STAR,
  input  BNEQ,
  input  BOVF,
  input  JNNG,
  input  JGRT,
  input  JMP,
  input  JSR,
  input  LD,
  input  ST,
  input  INC,
  input  SUB,
  input  TST,
  input  STRCPY,
  input  JADR,
  output [6:0] Adr6__0
);

  assign Adr6__0 = HALT ? 7'b0000010 : 7'bz;  // Controlled_Buffer controlled_buffer_1
  assign Adr6__0 = RTI ? 7'b0000011 : 7'bz;  // Controlled_Buffer controlled_buffer_2
  assign Adr6__0 = RTS ? 7'b0001011 : 7'bz;  // Controlled_Buffer controlled_buffer_3
  assign Adr6__0 = INTE ? 7'b0010010 : 7'bz;  // Controlled_Buffer controlled_buffer_4
  assign Adr6__0 = INTD ? 7'b0010011 : 7'bz;  // Controlled_Buffer controlled_buffer_5
  assign Adr6__0 = PUSH ? 7'b0010100 : 7'bz;  // Controlled_Buffer controlled_buffer_6
  assign Adr6__0 = POP ? 7'b0011001 : 7'bz;  // Controlled_Buffer controlled_buffer_7
  assign Adr6__0 = STBR ? 7'b0100010 : 7'bz;  // Controlled_Buffer controlled_buffer_8
  assign Adr6__0 = STXR ? 7'b0100011 : 7'bz;  // Controlled_Buffer controlled_buffer_9
  assign Adr6__0 = STAR ? 7'b0100100 : 7'bz;  // Controlled_Buffer controlled_buffer_10
  assign Adr6__0 = BNEQ ? 7'b0100110 : 7'bz;  // Controlled_Buffer controlled_buffer_11
  assign Adr6__0 = BOVF ? 7'b0100101 : 7'bz;  // Controlled_Buffer controlled_buffer_12
  assign Adr6__0 = JGRT ? 7'b0101001 : 7'bz;  // Controlled_Buffer controlled_buffer_13
  assign Adr6__0 = JNNG ? 7'b0101000 : 7'bz;  // Controlled_Buffer controlled_buffer_14
  assign Adr6__0 = JMP ? 7'b0101010 : 7'bz;  // Controlled_Buffer controlled_buffer_15
  assign Adr6__0 = JSR ? 7'b0101011 : 7'bz;  // Controlled_Buffer controlled_buffer_16
  assign Adr6__0 = LD ? 7'b0110000 : 7'bz;  // Controlled_Buffer controlled_buffer_17
  assign Adr6__0 = ST ? 7'b0110010 : 7'bz;  // Controlled_Buffer controlled_buffer_18
  assign Adr6__0 = INC ? 7'b0111000 : 7'bz;  // Controlled_Buffer controlled_buffer_19
  assign Adr6__0 = TST ? 7'b0111100 : 7'bz;  // Controlled_Buffer controlled_buffer_20
  assign Adr6__0 = SUB ? 7'b0111010 : 7'bz;  // Controlled_Buffer controlled_buffer_21
  assign Adr6__0 = STRCPY ? 7'b0111101 : 7'bz;  // Controlled_Buffer controlled_buffer_22
  assign Adr6__0 = JADR ? 7'b1000111 : 7'bz;  // Controlled_Buffer controlled_buffer_23
endmodule

module REG6_INC_LD (
  input  [5:0] I5__0,
  input  LD,
  input  INC,
  input  mr,
  input  CLK,
  output [5:0] A5__0
);

  wire reg2m_inc_ld_1_p7, reg2m_inc_ld_2_p8;

  // REG2m_INC_LD reg2m_inc_ld_1: pin names not known; wires that end beside it: CLK, mr, I5__0[5:4], A5__0[5:4], LD, INC, reg2m_inc_ld_1_p7
  // REG2m_INC_LD reg2m_inc_ld_2: pin names not known; wires that end beside it: CLK, reg2m_inc_ld_1_p7, mr, I5__0[3:2], A5__0[3:2], LD, INC, reg2m_inc_ld_2_p8
  // REG2m_INC_LD reg2m_inc_ld_3: pin names not known; wires that end beside it: CLK, reg2m_inc_ld_2_p8, mr, I5__0[1:0], A5__0[1:0], LD, INC, INC

  // Notes on the sheet:
  //   __
endmodule

module ROM_32x24 (
  input  [7:0] A8__0,
  input  CS,
  output [23:0] DOUT
);

  ROM #(.dataWidth(24)) rom_1 (.addr(A8__0), .data(DOUT), .sel(CS));
endmodule

module ALU16_ADD_SUB (
  input  Cin,
  input  [15:0] A,
  input  [15:0] B,
  input  add,
  input  sub,
  output [15:0] F,
  output Cout
);

  wire adder_1_cout, subtractor_1_bout;
  wire [15:0] adder_1_out, subtractor_1_out;

  Adder #(.width(16)) adder_1 (.a(A), .b(B), .out(adder_1_out), .cin(Cin), .cout(adder_1_cout));
  Subtractor #(.width(16)) subtractor_1 (.a(A), .b(B), .out(subtractor_1_out), .bin(Cin), .bout(subtractor_1_bout));
  assign F = add ? adder_1_out : 16'bz;  // Controlled_Buffer controlled_buffer_1
  assign Cout = add ? adder_1_cout : 1'bz;  // Controlled_Buffer controlled_buffer_2
  assign F = sub ? subtractor_1_out : 16'bz;  // Controlled_Buffer controlled_buffer_3
  assign Cout = sub ? subtractor_1_bout : 1'bz;  // Controlled_Buffer controlled_buffer_4
endmodule

module REG7_INC_LD (
  input  [6:0] I6__0,
  input  LD,
  input  INC,
  input  mr,
  input  CLK,
  output [6:0] A6__0
);

  wire reg2m_inc_ld_1_p7, reg2m_inc_ld_2_p8, reg2m_inc_ld_3_p8;

  // REG2m_INC_LD reg2m_inc_ld_1: pin names not known; wires that end beside it: CLK, mr, I6__0[6:5], A6__0[6:5], LD, INC, reg2m_inc_ld_1_p7
  // REG2m_INC_LD reg2m_inc_ld_2: pin names not known; wires that end beside it: CLK, reg2m_inc_ld_1_p7, mr, I6__0[4:3], A6__0[4:3], LD, INC, reg2m_inc_ld_2_p8
  // REG2m_INC_LD reg2m_inc_ld_3: pin names not known; wires that end beside it: CLK, reg2m_inc_ld_2_p8, mr, I6__0[2:1], A6__0[2:1], LD, INC, reg2m_inc_ld_3_p8
  // REG1m_INC_LD reg1m_inc_ld_1: pin names not known; wires that end beside it: CLK, reg2m_inc_ld_3_p8, mr, I6__0[0], A6__0[0], LD, INC, INC

  // Notes on the sheet:
  //   __
endmodule

module ROM_128x48 (
  input  [6:0] A7__0,
  input  CS,
  output [31:0] DOUT31__0,
  output [15:0] DOUT47__32
);

  ROM #(.addrWidth(7), .dataWidth(16)) rom_1 (.addr(A7__0), .data(DOUT47__32), .sel(CS));
  ROM #(.addrWidth(7), .dataWidth(32)) rom_2 (.addr(A7__0), .data(DOUT31__0), .sel(CS));
endmodule

module MP2_7b (
  input  En,
  input  [6:0] in_2,
  input  [6:0] in_3,
  input  S0,
  output [6:0] Y
);

  wire not_1_out;
  wire [6:0] and_1_out, and_2_out, bit_extender_1_out, bit_extender_2_out, bit_extender_3_out, or_1_out;

  Pull_Resistor #(.pull(1)) pull_resistor_1 (.node(En));
  assign bit_extender_1_out = {{6{S0}}, S0};  // Bit_Extender bit_extender_1
  assign bit_extender_2_out = {{6{not_1_out}}, not_1_out};  // Bit_Extender bit_extender_2
  not not_1 (not_1_out, S0);
  assign and_1_out = in_2 & bit_extender_2_out;  // AND_Gate and_1, 7 bits wide
  assign and_2_out = in_3 & bit_extender_1_out;  // AND_Gate and_2, 7 bits wide
  assign bit_extender_3_out = {{6{En}}, En};  // Bit_Extender bit_extender_3
  assign or_1_out = and_1_out | and_2_out;  // OR_Gate or_1, 7 bits wide
  assign Y = bit_extender_3_out & or_1_out;  // AND_Gate and_3, 7 bits wide

  // Notes on the sheet:
  //   I0
  //   6..0
  //   I1
  //   6..0
  //   Ako En nije priključen (stanje visoke impednase - HiZ),
  //   uezti za podrazumevanu vrednost logičku jedinicu
  //   6..0
endmodule

module ROM_32x21 (
  input  [4:0] A4__0,
  input  CS,
  output [20:0] DOUT
);

  ROM #(.addrWidth(5), .dataWidth(21)) rom_1 (.addr(A4__0), .data(DOUT), .sel(CS));
endmodule

module REG5_INC_LD (
  input  [4:0] I4__0,
  input  LD,
  input  INC,
  input  mr,
  input  CLK,
  output [4:0] A4__0
);

  wire reg4m_inc_ld_1_p7;

  // REG4m_INC_LD reg4m_inc_ld_1: pin names not known; wires that end beside it: CLK, mr, I4__0[4:1], A4__0[4:1], LD, INC, reg4m_inc_ld_1_p7
  // REG1m_INC_LD reg1m_inc_ld_1: pin names not known; wires that end beside it: CLK, reg4m_inc_ld_1_p7, mr, I4__0[0], A4__0[0], LD, INC, INC

  // Notes on the sheet:
  //   __
endmodule

module ROM_32x29 (
  input  [4:0] A4__0,
  input  CS,
  output [28:0] DOUT
);

  ROM #(.addrWidth(5), .dataWidth(29)) rom_1 (.addr(A4__0), .data(DOUT), .sel(CS));
endmodule
