// Logisim project ORT2Project.circ as structural Verilog: 8 circuits, main circuit COMPUTER
module COMPUTER (
);

  wire BTN_RST_out, CLK, cpu_1_inta, interrupt_interface_8_1_p4, interrupt_interface_8_1_p5,
       interrupt_interface_8_1_p6, interrupt_interface_8_1_p7, interrupt_interface_8_1_p8,
       interrupt_interface_8_1_p9, interrupt_interface_8_1_p10, interrupt_interface_8_1_p11,
       pull_resistor_1_node, pull_resistor_6_node, ram_1_out_8, rst;
  wire [2:0] cpu_1_uext2__0;
  wire [7:0] interrupt_interface_8_1_p1, pull_resistor_2_node, ram_1_out_7;
  wire [15:0] pull_resistor_3_node;

  Button BTN_RST (.out(BTN_RST_out));
  Clock u_CLK (.out(CLK));
  RisingEdge risingedge_1 (.INPUT(BTN_RST_out), .CLK(CLK), .OUTPUT(rst));
  RAM ram_1 (
    .in_1(pull_resistor_3_node), .in_2(CLK), .in_3(pull_resistor_2_node), .in_4(pull_resistor_1_node),
    .in_5(pull_resistor_6_node), .in_6(rst), .out_7(ram_1_out_7), .out_8(ram_1_out_8));
  Pull_Resistor pull_resistor_1 (.node(pull_resistor_1_node));
  Pull_Resistor pull_resistor_2 (.node(pull_resistor_2_node));
  Pull_Resistor pull_resistor_3 (.node(pull_resistor_3_node));
  Pull_Resistor pull_resistor_4 (.node(ram_1_out_7));
  Pull_Resistor pull_resistor_5 (.node(ram_1_out_8));
  Pull_Resistor pull_resistor_6 (.node(pull_resistor_6_node));
  CPU cpu_1 (
    .in_1(rst), .in_2(CLK), .in_3(ram_1_out_8), .in_4(ram_1_out_7), .ABUS(pull_resistor_3_node),
    .DOUTBUS(pull_resistor_2_node), .out_8(pull_resistor_1_node), .out_9(pull_resistor_6_node),
    .inta(cpu_1_inta), .intr7__0(interrupt_interface_8_1_p1), .UEXT2__0(cpu_1_uext2__0));
  // INTERRUPT_INTERFACE_8 interrupt_interface_8_1: pin names not known; wires that end beside it: interrupt_interface_8_1_p1, cpu_1_inta, cpu_1_uext2__0, interrupt_interface_8_1_p4, interrupt_interface_8_1_p5, interrupt_interface_8_1_p6, interrupt_interface_8_1_p7, interrupt_interface_8_1_p8, interrupt_interface_8_1_p9, interrupt_interface_8_1_p10, interrupt_interface_8_1_p11, CLK
  Button BTN_INTR7 (.out(interrupt_interface_8_1_p4));
  Button BTN_INTR6 (.out(interrupt_interface_8_1_p5));
  Button BTN_INTR5 (.out(interrupt_interface_8_1_p6));
  Button BTN_INTR4 (.out(interrupt_interface_8_1_p7));
  Button BTN_INTR3 (.out(interrupt_interface_8_1_p8));
  Button BTN_INTR2 (.out(interrupt_interface_8_1_p9));
  Button BTN_INTR1 (.out(interrupt_interface_8_1_p10));
  Button BTN_INTR0 (.out(interrupt_interface_8_1_p11));
endmodule

module CPU (
  input  in_1,
  input  in_2,
  input  in_3,
  input  [7:0] in_4,
  input  [7:0] intr7__0,
  output [15:0] ABUS,
  output [7:0] DOUTBUS,
  output out_8,
  output out_9,
  output inta,
  output [2:0] UEXT2__0
);

  wire [3:0] common_1_phaseffbus;
  wire [5:0] common_1_addrbus;
  wire [6:0] pull_resistor_3_node;
  wire [7:0] pull_resistor_7_node;
  wire [15:0] A, ALU, B, common_1_c, INTRADDR, PSW, pull_resistor_5_node;
  wire [22:0] common_1_instrucbus;
  wire [31:0] pull_resistor_6_node;

  COMMON common_1 (
    .CLK(in_2), .RST(in_1), .DIN(in_4), .CMEMBUS(pull_resistor_5_node), .MAR(ABUS), .MDR(DOUTBUS),
    .PHASEFFBUS(common_1_phaseffbus), .INSTRUCBUS(common_1_instrucbus), .ADDRBUS(common_1_addrbus),
    .PSW(PSW), .CREGBUS(pull_resistor_6_node), .CFFBUS(pull_resistor_7_node), .B(B), .A(A),
    .CPSW(pull_resistor_3_node), .ALU(ALU), .IVTPPDSP(INTRADDR), .C(common_1_c));
  Pull_Resistor pull_resistor_1 (.node(common_1_instrucbus));
  Pull_Resistor pull_resistor_2 (.node(common_1_phaseffbus));
  Pull_Resistor pull_resistor_3 (.node(pull_resistor_3_node));
  Pull_Resistor pull_resistor_4 (.node(common_1_addrbus));
  Pull_Resistor pull_resistor_5 (.node(pull_resistor_5_node));
  Pull_Resistor pull_resistor_6 (.node(pull_resistor_6_node));
  Pull_Resistor pull_resistor_7 (.node(pull_resistor_7_node));
  FETCH fetch_1 (
    .in_1(in_1), .in_2(in_2), .in_3(in_3), .PHASEFFBUS(common_1_phaseffbus),
    .INSTRUCBUS(common_1_instrucbus), .ADDRBUS(common_1_addrbus), .PSW(PSW), .rdMEM(out_9),
    .CMEMBUS(pull_resistor_5_node), .CFFBUS(pull_resistor_7_node), .CREGBUS(pull_resistor_6_node));
  ADDR addr_1 (
    .rdMEM(out_9), .CMEMBUS(pull_resistor_5_node), .CFFBUS(pull_resistor_7_node),
    .CREGBUS(pull_resistor_6_node), .INSTRUCBUS(common_1_instrucbus), .ADDRBUS(common_1_addrbus),
    .in_1(in_1), .in_2(in_2), .in_3(in_3), .PHASEFFBUS(common_1_phaseffbus));
  EXEC exec_1 (
    .in_1(in_1), .in_2(in_2), .in_3(in_3), .B(B), .PSW(PSW), .A(A), .ALU(ALU),
    .CMEMBUS(pull_resistor_5_node), .CFFBUS(pull_resistor_7_node), .CREGBUS(pull_resistor_6_node),
    .CPSW(pull_resistor_3_node), .rdMEM(out_9), .wrMEM(out_8), .PHASEFFBUS(common_1_phaseffbus),
    .INSTRUCBUS(common_1_instrucbus), .ADDRBUS(common_1_addrbus), .C(common_1_c));
  INTR intr_1 (
    .in_1(in_1), .in_2(in_2), .in_3(in_3), .PHASEFFBUS(common_1_phaseffbus), .PSW(PSW), .intr7__0(intr7__0),
    .ADDIVTP(INTRADDR), .CMEMBUS(pull_resistor_5_node), .CFFBUS(pull_resistor_7_node),
    .CREGBUS(pull_resistor_6_node), .rdMEM(out_9), .wrMEM(out_8), .UEXT2__0(UEXT2__0), .inta(inta),
    .INSTRUCBUS(common_1_instrucbus));

  // Other names for the same wires on the sheet: CLK = in_2; DIN7__0[7:0] = in_4; FCBUS = in_3; MAR[15:0] = ABUS;
  //   MDR[7:0] = DOUTBUS; RD = out_9; rst = in_1; WR = out_8
endmodule

module COMMON (
  input  CLK,
  input  RST,
  input  [7:0] DIN,
  input  [15:0] A,
  input  [15:0] ALU,
  input  [15:0] IVTPPDSP,
  input  [15:0] CMEMBUS,
  input  [7:0] CFFBUS,
  input  [31:0] CREGBUS,
  input  [6:0] CPSW,
  output [15:0] MAR,
  output [7:0] MDR,
  output [3:0] PHASEFFBUS,
  output [15:0] C,
  output [22:0] INSTRUCBUS,
  output [5:0] ADDRBUS,
  output [15:0] PSW,
  output [15:0] B
);

  wire A_ffff, adresna, and_30_out, and_31_out, and_32_out, and_33_out, and_34_out, and_35_out, and_36_out,
       and_37_out, and_38_out, and_39_out, and_40_out, and_41_out, and_42_out, and_43_out, and_44_out,
       and_45_out, and_46_out, and_47_out, and_48_out, and_49_out, and_50_out, and_51_out, and_52_out,
       and_53_out, and_55_out, and_56_out, and_57_out, and_58_out, ins_rst, instr, mp2_16b_3_p3,
       mp2_16b_3_p5, mp8_16b_1_p8, nor_1_out, not_1_out, not_2_out, not_3_out, not_4_out, not_5_out,
       not_6_out, not_7_out, not_8_out, not_9_out, not_10_out, or_4_out, or_5_out, or_6_out, or_7_out,
       or_8_out, or_9_out, or_10_out, or_12_out, or_13_out, or_14_out, or_15_out, or_16_out;
  wire [7:0] IR7__0, IR15__8, IR23__16, IR31__24, mp2_8b_1_out_5, mp8_8b_1_p8, PC7__0;
  wire [15:0] ADD1, ADD2, AR15__0, BR15__0, DR15__0, mp2_16b_1_out_5, mp2_16b_2_out_5, mp4_16b_1_y,
       mp4_16b_2_y, SP15__0, XR15__0;
  wire [15:8] PC15__0;

  REG8_LD reg8_ld_1 (.I7__0(MDR), .LD(CREGBUS[7]), .CLK(CLK), .A7__0(IR31__24));
  or or_1 (adresna, INSTRUCBUS[16], INSTRUCBUS[17], INSTRUCBUS[18], INSTRUCBUS[19], INSTRUCBUS[20], INSTRUCBUS[22], INSTRUCBUS[21]);
  // MP8_16b mp8_16b_1: pin names not known; wires that end beside it: CMEMBUS[9], CMEMBUS[5], CMEMBUS[6], {PC15__0, PC7__0}, {IR7__0, IR15__8}, AR15__0, ADD1, mp8_16b_1_p8, SP15__0, BR15__0, B, IVTPPDSP, 1'b1
  // REG16_INC_LD reg16_inc_ld_1: pin names not known; wires that end beside it: CLK, mp8_16b_1_p8, MAR, CMEMBUS[0], CMEMBUS[1]
  REG8_LD reg8_ld_2 (.I7__0(MDR), .LD(CREGBUS[6]), .CLK(CLK), .A7__0(IR23__16));
  MP2_16b mp2_16b_1 (.En(1'b1), .in_2(B), .in_3(BR15__0), .S0(CREGBUS[14]), .out_5(mp2_16b_1_out_5));
  MP4_16b mp4_16b_1 (
    .En(1'b1), .S0(CREGBUS[2]), .S1(CREGBUS[1]), .I0({IR7__0, IR15__8}), .I1(C), .I2(DR15__0), .I3(ADD1),
    .Y(mp4_16b_1_y));
  // REG16_INC_LD reg16_inc_ld_2: pin names not known; wires that end beside it: CLK, mp4_16b_1_y, B, DR15__0, CREGBUS[3]
  ADD16 add16_1 (.C0(1'b0), .A(mp2_16b_1_out_5), .B(mp2_16b_2_out_5), .F(ADD1));  // open: C16
  and and_1 (INSTRUCBUS[0], ~IR31__24[0], ~IR31__24[1], ~IR31__24[2], ~IR31__24[3], ~IR31__24[4], ~IR31__24[5], ~IR31__24[6], IR31__24[7]);  // AND_Gate
  and and_2 (INSTRUCBUS[1], IR31__24[0], ~IR31__24[1], ~IR31__24[2], ~IR31__24[3], ~IR31__24[4], ~IR31__24[5], ~IR31__24[6], IR31__24[7]);  // AND_Gate
  and and_3 (INSTRUCBUS[2], ~IR31__24[0], IR31__24[1], ~IR31__24[2], ~IR31__24[3], ~IR31__24[4], ~IR31__24[5], ~IR31__24[6], IR31__24[7]);  // AND_Gate
  and and_4 (INSTRUCBUS[3], IR31__24[0], IR31__24[1], ~IR31__24[2], ~IR31__24[3], ~IR31__24[4], ~IR31__24[5], ~IR31__24[6], IR31__24[7]);  // AND_Gate
  and and_5 (INSTRUCBUS[4], ~IR31__24[0], ~IR31__24[1], IR31__24[2], ~IR31__24[3], ~IR31__24[4], ~IR31__24[5], ~IR31__24[6], IR31__24[7]);  // AND_Gate
  and and_6 (INSTRUCBUS[5], IR31__24[0], ~IR31__24[1], IR31__24[2], ~IR31__24[3], ~IR31__24[4], ~IR31__24[5], ~IR31__24[6], IR31__24[7]);  // AND_Gate
  and and_7 (INSTRUCBUS[6], ~IR31__24[0], IR31__24[1], IR31__24[2], ~IR31__24[3], ~IR31__24[4], ~IR31__24[5], ~IR31__24[6], IR31__24[7]);  // AND_Gate
  and and_8 (INSTRUCBUS[7], IR31__24[0], IR31__24[1], IR31__24[2], ~IR31__24[3], ~IR31__24[4], ~IR31__24[5], ~IR31__24[6], IR31__24[7]);  // AND_Gate
  and and_9 (INSTRUCBUS[8], ~IR31__24[0], ~IR31__24[1], ~IR31__24[2], IR31__24[3], ~IR31__24[4], ~IR31__24[5], ~IR31__24[6], IR31__24[7]);  // AND_Gate
  and and_10 (INSTRUCBUS[9], IR31__24[0], ~IR31__24[1], ~IR31__24[2], IR31__24[3], ~IR31__24[4], ~IR31__24[5], ~IR31__24[6], IR31__24[7]);  // AND_Gate
  MP2_16b mp2_16b_2 (
    .En(1'b1), .in_2(XR15__0), .in_3({IR15__8, {8{IR15__8[7]}}}), .S0(CREGBUS[15]), .out_5(mp2_16b_2_out_5));
  REG8_LD reg8_ld_3 (.I7__0(MDR), .LD(CREGBUS[5]), .CLK(CLK), .A7__0(IR15__8));
  // MP8_8b mp8_8b_1: pin names not known; wires that end beside it: CMEMBUS[12], CMEMBUS[13], CMEMBUS[14], DIN, A[15:8], A[7:0], C[15:8], mp8_8b_1_p8, C[7:0], PC15__0, PC7__0, {PSW[15], {7{1'b0}}}, 1'b1
  MP2_8b mp2_8b_1 (.in_2(mp8_8b_1_p8), .in_3({3'b000, PSW[4:0]}), .S0(CMEMBUS[15]), .out_5(mp2_8b_1_out_5), .En(1'b1));
  REG8_LD reg8_ld_4 (.I7__0(mp2_8b_1_out_5), .LD(CMEMBUS[2]), .CLK(CLK), .A7__0(MDR));
  REG8_LD reg8_ld_5 (.I7__0(MDR), .LD(CREGBUS[8]), .CLK(CLK), .A7__0(C[15:8]));
  REG8_LD reg8_ld_6 (.I7__0(MDR), .LD(CREGBUS[4]), .CLK(CLK), .A7__0(IR7__0));
  and and_11 (INSTRUCBUS[10], ~IR31__24[0], ~IR31__24[1], ~IR31__24[2], ~IR31__24[3], ~IR31__24[4], ~IR31__24[5], IR31__24[6], IR31__24[7]);  // AND_Gate
  and and_12 (INSTRUCBUS[11], IR31__24[0], ~IR31__24[1], ~IR31__24[2], ~IR31__24[3], ~IR31__24[4], ~IR31__24[5], IR31__24[6], IR31__24[7]);  // AND_Gate
  and and_13 (INSTRUCBUS[12], ~IR31__24[0], IR31__24[1], ~IR31__24[2], ~IR31__24[3], ~IR31__24[4], ~IR31__24[5], IR31__24[6], IR31__24[7]);  // AND_Gate
  and and_14 (INSTRUCBUS[13], ~IR31__24[0], ~IR31__24[1], IR31__24[2], ~IR31__24[3], ~IR31__24[4], ~IR31__24[5], IR31__24[6], IR31__24[7]);  // AND_Gate
  and and_15 (INSTRUCBUS[14], ~IR31__24[0], ~IR31__24[1], ~IR31__24[2], ~IR31__24[3], ~IR31__24[4], ~IR31__24[5], IR31__24[6], ~IR31__24[7]);  // AND_Gate
  and and_16 (INSTRUCBUS[15], IR31__24[0], ~IR31__24[1], ~IR31__24[2], ~IR31__24[3], ~IR31__24[4], ~IR31__24[5], IR31__24[6], ~IR31__24[7]);  // AND_Gate
  and and_17 (INSTRUCBUS[16], ~IR31__24[0], ~IR31__24[1], ~IR31__24[2], ~IR31__24[3], IR31__24[4], IR31__24[5], ~IR31__24[6], ~IR31__24[7]);  // AND_Gate
  and and_18 (INSTRUCBUS[17], IR31__24[0], ~IR31__24[1], ~IR31__24[2], ~IR31__24[3], IR31__24[4], IR31__24[5], ~IR31__24[6], ~IR31__24[7]);  // AND_Gate
  and and_19 (INSTRUCBUS[18], ~IR31__24[0], IR31__24[1], ~IR31__24[2], ~IR31__24[3], IR31__24[4], IR31__24[5], ~IR31__24[6], ~IR31__24[7]);  // AND_Gate
  and and_20 (INSTRUCBUS[19], IR31__24[0], IR31__24[1], ~IR31__24[2], ~IR31__24[3], IR31__24[4], IR31__24[5], ~IR31__24[6], ~IR31__24[7]);  // AND_Gate
  ADD16 add16_2 (.C0(1'b0), .A({PC15__0, PC7__0}), .B({IR23__16, {8{IR23__16[7]}}}), .F(ADD2));  // open: C16
  REG8_LD reg8_ld_7 (.I7__0(MDR), .LD(CREGBUS[9]), .CLK(CLK), .A7__0(C[7:0]));
  MP4_16b mp4_16b_2 (
    .S0(CMEMBUS[11]), .S1(CMEMBUS[10]), .I0(MAR), .I1(ADD2), .I2({IR15__8, IR23__16}), .I3(C), .Y(mp4_16b_2_y));  // open: En
  not not_1 (not_1_out, RST);
  RSFF rsff_1 (.S(CFFBUS[0]), .CLK(CLK), .R(CFFBUS[1]), .Sd(not_1_out), .Q(PHASEFFBUS[0]));  // open: Rd, notQ
  // MP2_16b mp2_16b_3: pin names not known; wires that end beside it: RST, mp4_16b_2_y, mp2_16b_3_p3, 16'h1000, mp2_16b_3_p5
  // REG16_INC_LD reg16_inc_ld_3: pin names not known; wires that end beside it: CLK, mp2_16b_3_p3, {PC15__0, PC7__0}, CMEMBUS[4]
  and and_21 (INSTRUCBUS[20], ~IR31__24[0], ~IR31__24[1], IR31__24[2], ~IR31__24[3], IR31__24[4], IR31__24[5], ~IR31__24[6], ~IR31__24[7]);  // AND_Gate
  and and_22 (INSTRUCBUS[22], IR31__24[0], ~IR31__24[1], IR31__24[2], ~IR31__24[3], IR31__24[4], IR31__24[5], ~IR31__24[6], ~IR31__24[7]);  // AND_Gate
  and and_23 (INSTRUCBUS[21], ~IR31__24[0], IR31__24[1], IR31__24[2], ~IR31__24[3], IR31__24[4], IR31__24[5], ~IR31__24[6], ~IR31__24[7]);  // AND_Gate
  or or_2 (mp2_16b_3_p5, CMEMBUS[3], RST);
  and and_24 (ADDRBUS[0], ~IR23__16[0], ~IR23__16[1], ~IR23__16[2], ~IR23__16[3], adresna, ~IR23__16[4], ~IR23__16[5], ~IR23__16[6], ~IR23__16[7]);  // AND_Gate
  and and_25 (ADDRBUS[1], ~IR23__16[0], ~IR23__16[1], ~IR23__16[2], ~IR23__16[3], adresna, IR23__16[4], ~IR23__16[5], ~IR23__16[6], ~IR23__16[7]);  // AND_Gate
  and and_26 (ADDRBUS[2], ~IR23__16[0], ~IR23__16[1], ~IR23__16[2], ~IR23__16[3], adresna, ~IR23__16[4], IR23__16[5], ~IR23__16[6], ~IR23__16[7]);  // AND_Gate
  and and_27 (ADDRBUS[3], ~IR23__16[0], ~IR23__16[1], ~IR23__16[2], ~IR23__16[3], adresna, IR23__16[4], IR23__16[5], ~IR23__16[6], ~IR23__16[7]);  // AND_Gate
  and and_28 (ADDRBUS[4], ~IR23__16[0], ~IR23__16[1], ~IR23__16[2], ~IR23__16[3], adresna, ~IR23__16[4], ~IR23__16[5], IR23__16[6], ~IR23__16[7]);  // AND_Gate
  and and_29 (ADDRBUS[5], ~IR23__16[0], ~IR23__16[1], ~IR23__16[2], ~IR23__16[3], adresna, IR23__16[4], ~IR23__16[5], IR23__16[6], ~IR23__16[7]);  // AND_Gate
  RSFF rsff_2 (.S(CFFBUS[2]), .CLK(CLK), .R(CFFBUS[3]), .Rd(not_2_out), .Q(PHASEFFBUS[1]));  // open: Sd, notQ
  not not_2 (not_2_out, RST);
  or or_3 (instr, INSTRUCBUS[6], INSTRUCBUS[16], INSTRUCBUS[18], INSTRUCBUS[19]);
  or or_4 (or_4_out, A_ffff, and_30_out);
  and and_30 (and_30_out, ALU[15], ~A[15]);  // AND_Gate
  and and_31 (and_31_out, ALU[15], B[15], ~A[15]);  // AND_Gate
  or or_5 (or_5_out, and_31_out, and_32_out);
  and and_32 (and_32_out, ~ALU[15], ~B[15], A[15]);  // AND_Gate
  REG16_LD reg16_ld_1 (.I15__0(A), .LD(CREGBUS[10]), .CLK(CLK), .A15__0(AR15__0));
  REG16_LD reg16_ld_2 (.I15__0(A), .LD(CREGBUS[12]), .CLK(CLK), .A15__0(BR15__0));
  REG16 reg16_1 (
    .LD(RST), .A(16'hf000), .DEC(CMEMBUS[8]), .INC(CMEMBUS[7]), .CLK(CLK), .I(SP15__0));  // open: CL, SL, IL, SR, IR, Cout, Eout
  RSFF rsff_3 (.S(CFFBUS[4]), .CLK(CLK), .R(CFFBUS[5]), .Rd(not_3_out), .Q(PHASEFFBUS[2]));  // open: Sd, notQ
  not not_3 (not_3_out, RST);
  nor nor_1 (nor_1_out, A[0], A[1], A[2], A[3], A[4], A[5], A[6], A[7], A[8], A[9], A[10], A[11], A[12], A[13], A[14], A[15]);
  and and_33 (and_33_out, C[4], INSTRUCBUS[2]);
  and and_34 (and_34_out, CREGBUS[30], INSTRUCBUS[20]);
  and and_35 (and_35_out, instr, A[15]);
  and and_36 (and_36_out, C[2], INSTRUCBUS[2]);
  and and_37 (and_37_out, CREGBUS[31], or_6_out);
  or or_6 (or_6_out, INSTRUCBUS[18], INSTRUCBUS[19]);
  and and_38 (and_38_out, C[1], INSTRUCBUS[2]);
  and and_39 (and_39_out, INSTRUCBUS[18], or_4_out);
  and and_40 (and_40_out, INSTRUCBUS[19], or_5_out);
  and and_41 (and_41_out, ~C[0], INSTRUCBUS[2], CPSW[1]);  // AND_Gate
  and and_42 (and_42_out, C[0], INSTRUCBUS[2], CPSW[1]);
  and and_43 (and_43_out, C[3], INSTRUCBUS[2]);
  and and_44 (and_44_out, CREGBUS[29], INSTRUCBUS[20]);
  and and_45 (and_45_out, instr, nor_1_out);
  or or_7 (or_7_out, and_33_out, and_34_out, and_35_out);
  or or_8 (or_8_out, and_36_out, and_37_out);
  or or_9 (or_9_out, and_41_out, CPSW[0]);
  or or_10 (or_10_out, and_43_out, and_44_out, and_45_out);
  and and_46 (and_46_out, ~or_8_out, CPSW[4]);  // AND_Gate
  and and_47 (and_47_out, or_8_out, CPSW[4]);
  or or_11 (ins_rst, INSTRUCBUS[6], INSTRUCBUS[16], INSTRUCBUS[20]);
  or or_12 (or_12_out, and_38_out, and_39_out, and_40_out);
  RSFF rsff_4 (.S(CFFBUS[6]), .CLK(CLK), .R(CFFBUS[7]), .Rd(not_4_out), .Q(PHASEFFBUS[3]));  // open: Sd, notQ
  not not_4 (not_4_out, RST);
  and and_48 (and_48_out, ~or_10_out, CPSW[2]);  // AND_Gate
  and and_49 (and_49_out, or_10_out, CPSW[2]);
  and and_50 (and_50_out, ~or_7_out, CPSW[3]);  // AND_Gate
  and and_51 (and_51_out, or_7_out, CPSW[3]);
  or or_13 (or_13_out, ins_rst, and_46_out);
  and and_52 (and_52_out, ~or_12_out, CPSW[5]);  // AND_Gate
  and and_53 (and_53_out, or_12_out, CPSW[5]);
  REG16_LD reg16_ld_3 (.I15__0(16'h14fe), .LD(RST), .CLK(CLK), .A15__0(DR15__0));
  REG16_LD reg16_ld_4 (.I15__0(A), .LD(CREGBUS[13]), .CLK(CLK), .A15__0(XR15__0));
  not not_5 (not_5_out, RST);
  RSFF rsff_5 (.S(and_42_out), .CLK(CLK), .R(or_9_out), .Sd(not_5_out), .Q(PSW[0]));  // open: Rd, notQ
  RSFF rsff_6 (.S(and_49_out), .CLK(CLK), .R(and_48_out), .Rd(not_6_out), .Q(PSW[1]));  // open: Sd, notQ
  not not_6 (not_6_out, RST);
  RSFF rsff_7 (.S(and_51_out), .CLK(CLK), .R(and_50_out), .Rd(not_7_out), .Q(PSW[2]));  // open: Sd, notQ
  not not_7 (not_7_out, RST);
  RSFF rsff_8 (.S(and_47_out), .CLK(CLK), .R(or_13_out), .Rd(not_8_out), .Q(PSW[3]));  // open: Sd, notQ
  not not_8 (not_8_out, RST);
  or or_14 (or_14_out, ins_rst, and_52_out);
  and and_54 (A_ffff, A[0], A[1], A[2], A[3], A[4], A[5], A[6], A[7], A[8], A[9], A[10], A[11], A[12], A[13], A[14], A[15]);
  RSFF rsff_9 (.S(and_53_out), .CLK(CLK), .R(or_14_out), .Rd(not_9_out), .Q(PSW[4]));  // open: Sd, notQ
  not not_9 (not_9_out, RST);
  and and_55 (and_55_out, ~C[15], INSTRUCBUS[2]);  // AND_Gate
  or or_15 (or_15_out, and_55_out, INSTRUCBUS[4]);
  and and_56 (and_56_out, C[15], INSTRUCBUS[2]);
  or or_16 (or_16_out, and_56_out, INSTRUCBUS[3]);
  and and_57 (and_57_out, or_15_out, CPSW[6]);
  and and_58 (and_58_out, or_16_out, CPSW[6]);
  RSFF rsff_10 (.S(and_58_out), .CLK(CLK), .R(and_57_out), .Rd(not_10_out), .Q(PSW[15]));  // open: Sd, notQ
  not not_10 (not_10_out, RST);

  assign PSW[14:5] = {10{1'b0}};

  // Other names for the same wires on the sheet: A7__0[7:0] = A[7:0]; A15__0[15:0] = A; A15__8[7:0] = A[15:8];
  //   immed = ADDRBUS[0]; memdir = ADDRBUS[1]; regdir = ADDRBUS[2]; regind = ADDRBUS[3]; brpom = ADDRBUS[4];
  //   brxpom = ADDRBUS[5]; ALU15__0[15:0] = ALU; B15__0[15:0] = B; C7__0[7:0] = C[7:0]; C15__0[15:0] = C;
  //   C15__8[7:0] = C[15:8]; stFETCH = CFFBUS[0]; clFETCH = CFFBUS[1]; stADDR = CFFBUS[2]; clADDR = CFFBUS[3];
  //   stEXEC = CFFBUS[4]; clEXEC = CFFBUS[5]; stINTR = CFFBUS[6]; clINTR = CFFBUS[7]; ldMAR = CMEMBUS[0];
  //   incMAR = CMEMBUS[1]; ldMDR = CMEMBUS[2]; ldPC = CMEMBUS[3]; incPC = CMEMBUS[4]; mxMAR1 = CMEMBUS[5];
  //   mxMAR0 = CMEMBUS[6]; incSP = CMEMBUS[7]; decSP = CMEMBUS[8]; mxMAR2 = CMEMBUS[9]; mxPC1 = CMEMBUS[10];
  //   mxPC0 = CMEMBUS[11]; mxMDR2 = CMEMBUS[12]; mxMDR1 = CMEMBUS[13]; mxMDR0 = CMEMBUS[14]; mxMDR3 = CMEMBUS[15];
  //   clPSWSTART = CPSW[0]; ldSTART = CPSW[1]; ldZ = CPSW[2]; ldN = CPSW[3]; ldC = CPSW[4]; ldV = CPSW[5];
  //   ldI = CPSW[6]; mxB1 = CREGBUS[1]; mxB0 = CREGBUS[2]; ldB = CREGBUS[3]; ldIR7__0 = CREGBUS[4];
  //   ldIR15__8 = CREGBUS[5]; ldIR23__16 = CREGBUS[6]; ldIR31__24 = CREGBUS[7]; ldC15__8 = CREGBUS[8];
  //   ldC7__0 = CREGBUS[9]; ldAR = CREGBUS[10]; ldDR = CREGBUS[11]; ldBR = CREGBUS[12]; ldXR = CREGBUS[13];
  //   mxA = CREGBUS[14]; mxB = CREGBUS[15]; Z = CREGBUS[29]; N = CREGBUS[30]; c_t = CREGBUS[31]; Din7__0[7:0] = DIN;
  //   ENTRADDR15__0[15:0] = IVTPPDSP; HALT = INSTRUCBUS[0]; RTS = INSTRUCBUS[1]; RTI = INSTRUCBUS[2];
  //   INTE = INSTRUCBUS[3]; INTD = INSTRUCBUS[4]; PUSH = INSTRUCBUS[5]; POP = INSTRUCBUS[6]; STBR = INSTRUCBUS[7];
  //   STXR = INSTRUCBUS[8]; STAR = INSTRUCBUS[9]; BNEQ = INSTRUCBUS[10]; BOVF = INSTRUCBUS[11]; JNNG = INSTRUCBUS[12];
  //   JGRT = INSTRUCBUS[13]; JMP = INSTRUCBUS[14]; JSR = INSTRUCBUS[15]; LD = INSTRUCBUS[16]; ST = INSTRUCBUS[17];
  //   INC = INSTRUCBUS[18]; SUB = INSTRUCBUS[19]; TST = INSTRUCBUS[20]; JADR = INSTRUCBUS[21];
  //   STRCPY = INSTRUCBUS[22]; MAR15__0[15:0] = MAR; MDR7__0[7:0] = MDR; PC15__0[7:0] = PC7__0;
  //   PC15__8[7:0] = PC15__0; FETCH = PHASEFFBUS[0]; ADDR = PHASEFFBUS[1]; EXEC = PHASEFFBUS[2]; INTR = PHASEFFBUS[3];
  //   PSW7__0[4:0] = PSW[4:0]; PSW15__0 (some bits) = {PSW[15], PSW[4:0]}; PSWSTART = PSW[0]; PSWZ = PSW[1];
  //   PSWN = PSW[2]; PSWC = PSW[3]; PSWV = PSW[4]; PSW15__8[7] = PSW[15]; PSWI = PSW[15]

  // Notes on the sheet:
  //   MAR
  //   Pomoćni registri
  //   Sabirači
  //   Instrukcijski registar
  //   MDR
  //   Dekoderi za prepoznavanje instrukcije na osnovu sadrzaja registra IR23..16
  //   PC
  //   FF za pokretanje FETCH, ADDR, EXEC i INTR faze izvršavanja instrukcije
  //   Registri
  //   SP
  //   Programska statusna reč (PSW)
endmodule

module FETCH (
  input  in_1,
  input  in_2,
  input  in_3,
  input  [3:0] PHASEFFBUS,
  input  [22:0] INSTRUCBUS,
  input  [5:0] ADDRBUS,
  input  [15:0] PSW,
  output [15:0] CMEMBUS,
  output [7:0] CFFBUS,
  output [31:0] CREGBUS,
  output rdMEM
);

  wire addr2, addr3, addr4, addr_t, and_4_out, and_5_out, and_6_out, and_7_out, and_8_out, and_9_out,
       and_10_out, and_11_out, and_12_out, bezadr, bradr2, bradr3, brbezadr, brcnd, brjmp2, brjmp3,
       brnotFCBUS, bruncnd, clFETCH, grinst, incPC, jmp2, jmp3, ldIR7__0, ldIR15__8, ldIR23__16, ldIR31__24,
       ldMAR, ldMDR, nor_1_out, nor_2_out, not_1_out, not_2_out, not_3_out, not_4_out, not_5_out,
       notPSWSTARTandFETCH, or_3_out, or_6_out, or_7_out, or_8_out, or_9_out, or_10_out, or_12_out,
       or_13_out, rdMEM_t, stADDR, stEXEC;
  wire [3:0] rom_32x21_1_dout_2;
  wire [4:0] reg5_inc_ld_1_a4__0, rom_32x21_1_dout;
  wire [11:11] rom_32x21_1_dout_3;

  or or_1 (jmp2, INSTRUCBUS[10], INSTRUCBUS[11]);
  not not_1 (not_1_out, in_1);
  or or_2 (bezadr, INSTRUCBUS[0], INSTRUCBUS[1], INSTRUCBUS[2], INSTRUCBUS[3], INSTRUCBUS[4], INSTRUCBUS[5], INSTRUCBUS[6], INSTRUCBUS[7], INSTRUCBUS[8], INSTRUCBUS[9]);
  REG5_INC_LD reg5_inc_ld_1 (
    .I4__0(rom_32x21_1_dout), .LD(or_3_out), .INC(not_2_out), .mr(not_1_out), .CLK(in_2),
    .A4__0(reg5_inc_ld_1_a4__0));
  DC4_16 dc4_16_1 (
    .En(1'b1), .X3__0(rom_32x21_1_dout_2), .D1(bruncnd), .D2(notPSWSTARTandFETCH), .D3(brnotFCBUS),
    .D4(brbezadr), .D5(brjmp2), .D6(bradr2), .D7(brjmp3), .D8(bradr3));  // open: D0, D9, D10, D11, D12, D13, D14, D15
  not not_2 (not_2_out, or_3_out);
  ROM_32x21 rom_32x21_1 (
    .A4__0(reg5_inc_ld_1_a4__0), .CS(1'b1),
    .DOUT({rom_32x21_1_dout, rom_32x21_1_dout_2, rom_32x21_1_dout_3[11], stEXEC, stADDR, clFETCH, ldIR7__0, ldIR15__8, ldIR23__16, ldIR31__24, ldMDR, rdMEM_t, incPC, ldMAR}));
  or or_3 (or_3_out, brcnd, bruncnd);
  or or_4 (jmp3, INSTRUCBUS[12], INSTRUCBUS[13], INSTRUCBUS[14], INSTRUCBUS[15]);
  or or_5 (addr_t, INSTRUCBUS[16], INSTRUCBUS[17], INSTRUCBUS[18], INSTRUCBUS[19], INSTRUCBUS[20], INSTRUCBUS[22], INSTRUCBUS[21]);
  or or_6 (or_6_out, ADDRBUS[2], ADDRBUS[3]);
  or or_7 (or_7_out, ADDRBUS[4], ADDRBUS[5]);
  or or_8 (or_8_out, ADDRBUS[0], ADDRBUS[1]);
  and and_1 (addr2, addr_t, or_6_out);
  and and_2 (addr3, addr_t, or_7_out);
  and and_3 (addr4, addr_t, or_8_out);
  not not_3 (not_3_out, PHASEFFBUS[0]);
  not not_4 (not_4_out, PSW[0]);
  or or_9 (or_9_out, not_3_out, not_4_out);
  not not_5 (not_5_out, in_3);
  and and_4 (and_4_out, or_9_out, notPSWSTARTandFETCH);
  and and_5 (and_5_out, bezadr, brbezadr);
  and and_6 (and_6_out, jmp2, brjmp2);
  and and_7 (and_7_out, addr2, bradr2);
  and and_8 (and_8_out, addr3, bradr3);
  and and_9 (and_9_out, jmp3, brjmp3);
  and and_10 (and_10_out, not_5_out, brnotFCBUS);
  nor nor_1 (nor_1_out, INSTRUCBUS[0], INSTRUCBUS[1], INSTRUCBUS[2], INSTRUCBUS[3], INSTRUCBUS[4], INSTRUCBUS[5], INSTRUCBUS[6], INSTRUCBUS[7], INSTRUCBUS[8], INSTRUCBUS[9], INSTRUCBUS[10], INSTRUCBUS[11], INSTRUCBUS[12], INSTRUCBUS[13], INSTRUCBUS[14], INSTRUCBUS[15], INSTRUCBUS[16], INSTRUCBUS[17], INSTRUCBUS[18], INSTRUCBUS[19], INSTRUCBUS[20], INSTRUCBUS[22], INSTRUCBUS[21]);
  or or_10 (or_10_out, ADDRBUS[2], ADDRBUS[0]);
  or or_11 (brcnd, and_4_out, and_5_out, and_6_out, and_7_out, and_8_out, and_9_out, and_10_out);
  or or_12 (or_12_out, INSTRUCBUS[17], INSTRUCBUS[7], INSTRUCBUS[8], INSTRUCBUS[9]);
  and and_11 (and_11_out, or_12_out, ADDRBUS[0]);
  and and_12 (and_12_out, INSTRUCBUS[21], or_10_out);
  nor nor_2 (nor_2_out, ADDRBUS[0], ADDRBUS[1], ADDRBUS[2], ADDRBUS[3], ADDRBUS[4], ADDRBUS[5]);
  or or_13 (or_13_out, and_11_out, and_12_out);
  assign CMEMBUS[0] = ldMAR ? 1'b1 : 1'bz;  // Controlled_Buffer controlled_buffer_1
  assign CMEMBUS[2] = ldMDR ? 1'b1 : 1'bz;  // Controlled_Buffer controlled_buffer_2
  assign CMEMBUS[4] = incPC ? 1'b1 : 1'bz;  // Controlled_Buffer controlled_buffer_3
  assign CFFBUS[1] = clFETCH ? 1'b1 : 1'bz;  // Controlled_Buffer controlled_buffer_4
  assign CFFBUS[2] = stADDR ? 1'b1 : 1'bz;  // Controlled_Buffer controlled_buffer_5
  assign CFFBUS[4] = stEXEC ? 1'b1 : 1'bz;  // Controlled_Buffer controlled_buffer_6
  assign CREGBUS[4] = ldIR7__0 ? 1'b1 : 1'bz;  // Controlled_Buffer controlled_buffer_7
  assign CREGBUS[5] = ldIR15__8 ? 1'b1 : 1'bz;  // Controlled_Buffer controlled_buffer_8
  assign CREGBUS[6] = ldIR23__16 ? 1'b1 : 1'bz;  // Controlled_Buffer controlled_buffer_9
  assign CREGBUS[7] = ldIR31__24 ? 1'b1 : 1'bz;  // Controlled_Buffer controlled_buffer_10
  or or_14 (grinst, nor_2_out, nor_1_out, or_13_out);
  assign rdMEM = rdMEM_t ? 1'b1 : 1'bz;  // Controlled_Buffer controlled_buffer_11

  // Other names for the same wires on the sheet: immed = ADDRBUS[0]; memdir = ADDRBUS[1]; regdir = ADDRBUS[2];
  //   regind = ADDRBUS[3]; brpom = ADDRBUS[4]; brxpom = ADDRBUS[5]; CLK = in_2; FCBUS = in_3; HALT = INSTRUCBUS[0];
  //   RTS = INSTRUCBUS[1]; RTI = INSTRUCBUS[2]; INTE = INSTRUCBUS[3]; INTD = INSTRUCBUS[4]; PUSH = INSTRUCBUS[5];
  //   POP = INSTRUCBUS[6]; STBR = INSTRUCBUS[7]; STXR = INSTRUCBUS[8]; STAR = INSTRUCBUS[9]; BNEQ = INSTRUCBUS[10];
  //   BOVF = INSTRUCBUS[11]; JNNG = INSTRUCBUS[12]; JGRT = INSTRUCBUS[13]; JMP = INSTRUCBUS[14]; JSR = INSTRUCBUS[15];
  //   LD = INSTRUCBUS[16]; ST = INSTRUCBUS[17]; INC = INSTRUCBUS[18]; SUB = INSTRUCBUS[19]; TST = INSTRUCBUS[20];
  //   JADR = INSTRUCBUS[21]; STRCPY = INSTRUCBUS[22]; FETCH = PHASEFFBUS[0]; ADDR = PHASEFFBUS[1];
  //   EXEC = PHASEFFBUS[2]; INTR = PHASEFFBUS[3]; PSWSTART = PSW[0]; rst = in_1

  // Notes on the sheet:
  //   Operaciona jedinica
  //   Kontrolna jedinica
endmodule

module ADDR (
  input  in_1,
  input  in_2,
  input  in_3,
  input  [3:0] PHASEFFBUS,
  input  [22:0] INSTRUCBUS,
  input  [5:0] ADDRBUS,
  output [15:0] CMEMBUS,
  output [7:0] CFFBUS,
  output [31:0] CREGBUS,
  output rdMEM
);

  wire and_1_out, and_2_out, and_3_out, and_4_out, and_5_out, bradr, brcnd, brgrinst, brnotADDR, brnotFCBUS,
       bruncnd, clADDR, grinst, incMAR, ldB, ldC7__0, ldC15__8, ldMAR, ldMDR, mxA, mxB, mxB0, mxB1, mxMAR0,
       mxMAR1, nor_1_out, nor_2_out, not_1_out, not_3_out, not_4_out, or_2_out, or_3_out, or_4_out, rdMEM_t,
       reg8_inc_ld_1_p5, reg8_inc_ld_1_p6, stEXEC, stFETCH;
  wire [4:0] kmadr_1_adr4__0;
  wire [7:0] mp2_8b_1_out_5, reg8_inc_ld_1_p4;
  wire [23:16] rom_32x24_1_dout;

  not not_1 (not_1_out, in_1);
  DC3_8 dc3_8_1 (
    .En(1'b1), .X2__0(rom_32x24_1_dout[18:16]), .D1(bruncnd), .D2(brgrinst), .D3(brnotFCBUS), .D4(brnotADDR),
    .D5(bradr));  // open: D0, D6, D7
  KMADR kmadr_1 (
    .immed(ADDRBUS[0]), .memdir(ADDRBUS[1]), .regdir(ADDRBUS[2]), .regind(ADDRBUS[3]),
    .Adr4__0(kmadr_1_adr4__0), .brpom(ADDRBUS[5]), .brxpom(ADDRBUS[4]));
  MP2_8b mp2_8b_1 (
    .in_2({3'b000, rom_32x24_1_dout[23:19]}), .in_3({3'b000, kmadr_1_adr4__0}), .S0(bradr),
    .out_5(mp2_8b_1_out_5));  // open: En
  // REG8_INC_LD reg8_inc_ld_1: pin names not known; wires that end beside it: in_2, not_1_out, mp2_8b_1_out_5, reg8_inc_ld_1_p4, reg8_inc_ld_1_p5, reg8_inc_ld_1_p6
  ROM_32x24 rom_32x24_1 (
    .A8__0(reg8_inc_ld_1_p4), .CS(1'b1),
    .DOUT({rom_32x24_1_dout, stEXEC, clADDR, stFETCH, mxB, mxA, mxB1, mxB0, rdMEM_t, ldMDR, ldC7__0, ldC15__8, incMAR, mxMAR1, mxMAR0, ldMAR, ldB}));
  not not_2 (reg8_inc_ld_1_p6, reg8_inc_ld_1_p5);
  or or_1 (reg8_inc_ld_1_p5, brcnd, bruncnd, bradr);
  nor nor_1 (nor_1_out, INSTRUCBUS[0], INSTRUCBUS[1], INSTRUCBUS[2], INSTRUCBUS[3], INSTRUCBUS[4], INSTRUCBUS[5], INSTRUCBUS[6], INSTRUCBUS[7], INSTRUCBUS[8], INSTRUCBUS[9], INSTRUCBUS[10], INSTRUCBUS[11], INSTRUCBUS[12], INSTRUCBUS[13], INSTRUCBUS[14], INSTRUCBUS[15], INSTRUCBUS[16], INSTRUCBUS[17], INSTRUCBUS[18], INSTRUCBUS[19], INSTRUCBUS[20], INSTRUCBUS[22], INSTRUCBUS[21]);
  or or_2 (or_2_out, ADDRBUS[2], ADDRBUS[0]);
  not not_3 (not_3_out, in_3);
  not not_4 (not_4_out, PHASEFFBUS[1]);
  nor nor_2 (nor_2_out, ADDRBUS[0], ADDRBUS[1], ADDRBUS[2], ADDRBUS[3], ADDRBUS[4], ADDRBUS[5]);
  or or_3 (or_3_out, INSTRUCBUS[17], INSTRUCBUS[7], INSTRUCBUS[8], INSTRUCBUS[9]);
  and and_1 (and_1_out, or_3_out, ADDRBUS[0]);
  and and_2 (and_2_out, INSTRUCBUS[21], or_2_out);
  and and_3 (and_3_out, brgrinst, grinst);
  and and_4 (and_4_out, brnotFCBUS, not_3_out);
  and and_5 (and_5_out, brnotADDR, not_4_out);
  or or_4 (or_4_out, and_1_out, and_2_out);
  or or_5 (brcnd, and_3_out, and_4_out, and_5_out);
  or or_6 (grinst, nor_2_out, nor_1_out, or_4_out);
  assign CMEMBUS[0] = ldMAR ? 1'b1 : 1'bz;  // Controlled_Buffer controlled_buffer_1
  assign CMEMBUS[1] = incMAR ? 1'b1 : 1'bz;  // Controlled_Buffer controlled_buffer_2
  assign CMEMBUS[2] = ldMDR ? 1'b1 : 1'bz;  // Controlled_Buffer controlled_buffer_3
  assign CMEMBUS[5] = mxMAR1 ? 1'b1 : 1'bz;  // Controlled_Buffer controlled_buffer_4
  assign CMEMBUS[6] = mxMAR0 ? 1'b1 : 1'bz;  // Controlled_Buffer controlled_buffer_5
  assign CFFBUS[0] = stFETCH ? 1'b1 : 1'bz;  // Controlled_Buffer controlled_buffer_6
  assign CFFBUS[3] = clADDR ? 1'b1 : 1'bz;  // Controlled_Buffer controlled_buffer_7
  assign CFFBUS[4] = stEXEC ? 1'b1 : 1'bz;  // Controlled_Buffer controlled_buffer_8
  assign CREGBUS[1] = mxB1 ? 1'b1 : 1'bz;  // Controlled_Buffer controlled_buffer_9
  assign CREGBUS[2] = mxB0 ? 1'b1 : 1'bz;  // Controlled_Buffer controlled_buffer_10
  assign CREGBUS[3] = ldB ? 1'b1 : 1'bz;  // Controlled_Buffer controlled_buffer_11
  assign CREGBUS[8] = ldC15__8 ? 1'b1 : 1'bz;  // Controlled_Buffer controlled_buffer_12
  assign CREGBUS[9] = ldC7__0 ? 1'b1 : 1'bz;  // Controlled_Buffer controlled_buffer_13
  assign CREGBUS[14] = mxA ? 1'b1 : 1'bz;  // Controlled_Buffer controlled_buffer_14
  assign CREGBUS[15] = mxB ? 1'b1 : 1'bz;  // Controlled_Buffer controlled_buffer_15
  assign rdMEM = rdMEM_t ? 1'b1 : 1'bz;  // Controlled_Buffer controlled_buffer_16

  // Other names for the same wires on the sheet: immed = ADDRBUS[0]; memdir = ADDRBUS[1]; regdir = ADDRBUS[2];
  //   regind = ADDRBUS[3]; brpom = ADDRBUS[4]; brxpom = ADDRBUS[5]; CLK = in_2; FCBUS = in_3; HALT = INSTRUCBUS[0];
  //   RTS = INSTRUCBUS[1]; RTI = INSTRUCBUS[2]; INTE = INSTRUCBUS[3]; INTD = INSTRUCBUS[4]; PUSH = INSTRUCBUS[5];
  //   POP = INSTRUCBUS[6]; STBR = INSTRUCBUS[7]; STXR = INSTRUCBUS[8]; STAR = INSTRUCBUS[9]; BNEQ = INSTRUCBUS[10];
  //   BOVF = INSTRUCBUS[11]; JNNG = INSTRUCBUS[12]; JGRT = INSTRUCBUS[13]; JMP = INSTRUCBUS[14]; JSR = INSTRUCBUS[15];
  //   LD = INSTRUCBUS[16]; ST = INSTRUCBUS[17]; INC = INSTRUCBUS[18]; SUB = INSTRUCBUS[19]; TST = INSTRUCBUS[20];
  //   JADR = INSTRUCBUS[21]; STRCPY = INSTRUCBUS[22]; FETCH = PHASEFFBUS[0]; ADDR = PHASEFFBUS[1];
  //   EXEC = PHASEFFBUS[2]; INTR = PHASEFFBUS[3]; rst = in_1

  // Notes on the sheet:
  //   Operaciona jedinica
  //   Upravljacka jedinica
endmodule

module EXEC (
  input  in_1,
  input  in_2,
  input  in_3,
  input  [15:0] B,
  input  [15:0] C,
  input  [3:0] PHASEFFBUS,
  input  [22:0] INSTRUCBUS,
  input  [5:0] ADDRBUS,
  input  [15:0] PSW,
  output [15:0] A,
  output [15:0] ALU,
  output [15:0] CMEMBUS,
  output [7:0] CFFBUS,
  output [31:0] CREGBUS,
  output [6:0] CPSW,
  output rdMEM,
  output wrMEM
);

  wire add, and_1_out, and_2_out, and_4_out, and_5_out, and_6_out, and_7_out, and_8_out, and_9_out,
       and_10_out, and_11_out, and_12_out, and_13_out, and_14_out, and_15_out, and_16_out, and_17_out,
       and_18_out, and_19_out, and_20_out, and_21_out, and_22_out, and_23_out, and_24_out, brcnd,
       brnotbrorjmp, brnotEXEC, brnotFCBUS, bropr, brorjmp, brregdir, bruncnd, clEXEC, clPSWSTART, decSP,
       incMAR, incSP, ldA, ldAR, ldBR, ldC, ldC7__0, ldC15__8, ldDR, ldI, ldMAR, ldMDR, ldN, ldPC, ldSTART,
       ldV, ldXR, ldZ, mp4_16b_1_p5, mxA0, mxA1, mxALU0, mxMAR0, mxMAR1, mxMAR2, mxMDR0, mxMDR1, mxMDR2,
       mxPC0, mxPC1, N, not_1_out, not_2_out, not_3_out, not_4_out, not_5_out, not_6_out, not_7_out,
       not_8_out, or_1_out, or_3_out, rdMEM_t, stINTR, sub_t, wrMEM_t, xor_1_out, Z;
  wire [2:0] rom_128x48_1_dout47__32_2;
  wire [6:0] kmopr_1_adr6__0, mp2_7b_1_y, reg7_inc_ld_1_a6__0, rom_128x48_1_dout47__32;
  wire [15:0] mp2_16b_1_out_5;
  wire [27:27] rom_128x48_1_dout31__0;

  // MP4_16b mp4_16b_1: pin names not known; wires that end beside it: mxA1, mxA0, C, B, mp4_16b_1_p5, ALU, ldA, 1'b1
  // REG16_CL_LD reg16_cl_ld_1: pin names not known; wires that end beside it: in_2, mp4_16b_1_p5, A, ldA, in_1
  not not_1 (not_1_out, in_1);
  MP2_16b mp2_16b_1 (.En(1'b1), .in_2(B), .in_3(16'h1), .S0(mxALU0), .out_5(mp2_16b_1_out_5));
  ALU16_ADD_SUB alu16_add_sub_1 (
    .Cin(PSW[3]), .A(A), .B(mp2_16b_1_out_5), .add(add), .sub(sub_t), .F(ALU), .Cout(CREGBUS[31]));
  MP2_7b mp2_7b_1 (.En(1'b1), .in_2(rom_128x48_1_dout47__32), .in_3(kmopr_1_adr6__0), .S0(bropr), .Y(mp2_7b_1_y));
  REG7_INC_LD reg7_inc_ld_1 (
    .I6__0(mp2_7b_1_y), .LD(or_1_out), .INC(not_2_out), .mr(not_1_out), .CLK(in_2),
    .A6__0(reg7_inc_ld_1_a6__0));
  not not_2 (not_2_out, or_1_out);
  KMOPR kmopr_1 (
    .HALT(INSTRUCBUS[0]), .RTI(INSTRUCBUS[2]), .RTS(INSTRUCBUS[1]), .INTE(INSTRUCBUS[3]),
    .INTD(INSTRUCBUS[4]), .PUSH(INSTRUCBUS[5]), .POP(INSTRUCBUS[6]), .STBR(INSTRUCBUS[7]),
    .STXR(INSTRUCBUS[8]), .STAR(INSTRUCBUS[9]), .BNEQ(INSTRUCBUS[10]), .Adr6__0(kmopr_1_adr6__0),
    .BOVF(INSTRUCBUS[11]), .JNNG(INSTRUCBUS[12]), .JGRT(INSTRUCBUS[13]), .JMP(INSTRUCBUS[14]),
    .JSR(INSTRUCBUS[15]), .LD(INSTRUCBUS[16]), .ST(INSTRUCBUS[17]), .INC(INSTRUCBUS[18]),
    .SUB(INSTRUCBUS[19]), .TST(INSTRUCBUS[20]), .STRCPY(INSTRUCBUS[22]), .JADR(INSTRUCBUS[21]));
  or or_1 (or_1_out, bruncnd, bropr, brcnd);
  ROM_128x48 rom_128x48_1 (
    .A7__0(reg7_inc_ld_1_a6__0), .CS(1'b1),
    .DOUT47__32({rom_128x48_1_dout47__32, rom_128x48_1_dout47__32_2, clEXEC, stINTR, ldDR, sub_t, add, mxALU0}),
    .DOUT31__0({incMAR, mxA1, mxA0, ldAR, rom_128x48_1_dout31__0[27], ldXR, ldBR, ldA, wrMEM_t, ldI, ldV, ldC, ldZ, ldN, ldSTART, mxPC1, mxPC0, ldPC, ldC15__8, ldC7__0, mxMDR2, mxMDR1, mxMDR0, rdMEM_t, ldMDR, mxMAR2, mxMAR1, mxMAR0, ldMAR, decSP, incSP, clPSWSTART}));
  and and_1 (and_1_out, A[13], B[13]);
  and and_2 (and_2_out, A[14], B[14]);
  and and_3 (N, A[15], B[15]);
  DC3_8 dc3_8_1 (
    .En(1'b1), .X2__0(rom_128x48_1_dout47__32_2), .D1(bropr), .D2(brnotEXEC), .D3(brnotFCBUS),
    .D4(brnotbrorjmp), .D5(brregdir), .D6(bruncnd));  // open: D0, D7
  and and_4 (and_4_out, A[11], B[11]);
  and and_5 (and_5_out, A[12], B[12]);
  and and_6 (and_6_out, A[10], B[10]);
  and and_7 (and_7_out, A[8], B[8]);
  and and_8 (and_8_out, A[9], B[9]);
  nor nor_1 (Z, N, and_2_out, and_1_out, and_5_out, and_4_out, and_6_out, and_8_out, and_7_out, and_10_out, and_11_out, and_9_out, and_13_out, and_12_out, and_14_out, and_16_out, and_15_out);
  and and_9 (and_9_out, A[5], B[5]);
  and and_10 (and_10_out, A[7], B[7]);
  and and_11 (and_11_out, A[6], B[6]);
  and and_12 (and_12_out, A[3], B[3]);
  and and_13 (and_13_out, A[4], B[4]);
  and and_14 (and_14_out, A[2], B[2]);
  and and_15 (and_15_out, A[0], B[0]);
  and and_16 (and_16_out, A[1], B[1]);
  not not_3 (not_3_out, PHASEFFBUS[2]);
  not not_4 (not_4_out, in_3);
  not not_5 (not_5_out, brorjmp);
  and and_17 (and_17_out, not_3_out, brnotEXEC);
  and and_18 (and_18_out, not_4_out, brnotFCBUS);
  and and_19 (and_19_out, not_5_out, brnotbrorjmp);
  and and_20 (and_20_out, ADDRBUS[2], brregdir);
  xor xor_1 (xor_1_out, PSW[4], PSW[2]);
  or or_2 (brcnd, and_17_out, and_18_out, and_19_out, and_20_out);
  not not_6 (not_6_out, PSW[1]);
  not not_7 (not_7_out, PSW[2]);
  or or_3 (or_3_out, xor_1_out, PSW[1]);
  not not_8 (not_8_out, or_3_out);
  and and_21 (and_21_out, not_6_out, INSTRUCBUS[10]);
  and and_22 (and_22_out, PSW[4], INSTRUCBUS[11]);
  and and_23 (and_23_out, not_7_out, INSTRUCBUS[12]);
  and and_24 (and_24_out, not_8_out, INSTRUCBUS[13]);
  or or_4 (brorjmp, and_21_out, and_22_out, and_23_out, and_24_out);
  assign CMEMBUS[0] = ldMAR ? 1'b1 : 1'bz;  // Controlled_Buffer controlled_buffer_1
  assign CMEMBUS[1] = incMAR ? 1'b1 : 1'bz;  // Controlled_Buffer controlled_buffer_2
  assign CMEMBUS[2] = ldMDR ? 1'b1 : 1'bz;  // Controlled_Buffer controlled_buffer_3
  assign CMEMBUS[3] = ldPC ? 1'b1 : 1'bz;  // Controlled_Buffer controlled_buffer_4
  assign CMEMBUS[5] = mxMAR1 ? 1'b1 : 1'bz;  // Controlled_Buffer controlled_buffer_5
  assign CMEMBUS[6] = mxMAR0 ? 1'b1 : 1'bz;  // Controlled_Buffer controlled_buffer_6
  assign CMEMBUS[7] = incSP ? 1'b1 : 1'bz;  // Controlled_Buffer controlled_buffer_7
  assign CMEMBUS[8] = decSP ? 1'b1 : 1'bz;  // Controlled_Buffer controlled_buffer_8
  assign CMEMBUS[9] = mxMAR2 ? 1'b1 : 1'bz;  // Controlled_Buffer controlled_buffer_9
  assign CMEMBUS[10] = mxPC1 ? 1'b1 : 1'bz;  // Controlled_Buffer controlled_buffer_10
  assign CMEMBUS[11] = mxPC0 ? 1'b1 : 1'bz;  // Controlled_Buffer controlled_buffer_11
  assign CMEMBUS[12] = mxMDR2 ? 1'b1 : 1'bz;  // Controlled_Buffer controlled_buffer_12
  assign CMEMBUS[13] = mxMDR1 ? 1'b1 : 1'bz;  // Controlled_Buffer controlled_buffer_13
  assign CMEMBUS[14] = mxMDR0 ? 1'b1 : 1'bz;  // Controlled_Buffer controlled_buffer_14
  assign CREGBUS[8] = ldC15__8 ? 1'b1 : 1'bz;  // Controlled_Buffer controlled_buffer_15
  assign CREGBUS[9] = ldC7__0 ? 1'b1 : 1'bz;  // Controlled_Buffer controlled_buffer_16
  assign CREGBUS[10] = ldAR ? 1'b1 : 1'bz;  // Controlled_Buffer controlled_buffer_17
  assign CREGBUS[11] = ldDR ? 1'b1 : 1'bz;  // Controlled_Buffer controlled_buffer_18
  assign CREGBUS[12] = ldBR ? 1'b1 : 1'bz;  // Controlled_Buffer controlled_buffer_19
  assign CREGBUS[13] = ldXR ? 1'b1 : 1'bz;  // Controlled_Buffer controlled_buffer_20
  assign CREGBUS[29] = Z ? 1'b1 : 1'bz;  // Controlled_Buffer controlled_buffer_21
  assign CREGBUS[30] = N ? 1'b1 : 1'bz;  // Controlled_Buffer controlled_buffer_22
  assign CPSW[0] = clPSWSTART ? 1'b1 : 1'bz;  // Controlled_Buffer controlled_buffer_23
  assign CPSW[1] = ldSTART ? 1'b1 : 1'bz;  // Controlled_Buffer controlled_buffer_24
  assign CPSW[2] = ldZ ? 1'b1 : 1'bz;  // Controlled_Buffer controlled_buffer_25
  assign CPSW[3] = ldN ? 1'b1 : 1'bz;  // Controlled_Buffer controlled_buffer_26
  assign CPSW[4] = ldC ? 1'b1 : 1'bz;  // Controlled_Buffer controlled_buffer_27
  assign CPSW[5] = ldV ? 1'b1 : 1'bz;  // Controlled_Buffer controlled_buffer_28
  assign CPSW[6] = ldI ? 1'b1 : 1'bz;  // Controlled_Buffer controlled_buffer_29
  assign CFFBUS[5] = clEXEC ? 1'b1 : 1'bz;  // Controlled_Buffer controlled_buffer_30
  assign CFFBUS[6] = stINTR ? 1'b1 : 1'bz;  // Controlled_Buffer controlled_buffer_31
  assign rdMEM = rdMEM_t ? 1'b1 : 1'bz;  // Controlled_Buffer controlled_buffer_32
  assign wrMEM = wrMEM_t ? 1'b1 : 1'bz;  // Controlled_Buffer controlled_buffer_33

  // Other names for the same wires on the sheet: A15__0[15:0] = A; memdir = ADDRBUS[0]; immed = ADDRBUS[1];
  //   regdir = ADDRBUS[2]; regind = ADDRBUS[3]; brpom = ADDRBUS[4]; brxpom = ADDRBUS[5]; ALU15__0[15:0] = ALU;
  //   B15__0[15:0] = B; C15__0[15:0] = C; CLK = in_2; c_t = CREGBUS[31]; FCBUS = in_3; HALT = INSTRUCBUS[0];
  //   RTS = INSTRUCBUS[1]; RTI = INSTRUCBUS[2]; INTE = INSTRUCBUS[3]; INTD = INSTRUCBUS[4]; PUSH = INSTRUCBUS[5];
  //   POP = INSTRUCBUS[6]; STBR = INSTRUCBUS[7]; STXR = INSTRUCBUS[8]; STAR = INSTRUCBUS[9]; BNEQ = INSTRUCBUS[10];
  //   BOVF = INSTRUCBUS[11]; JNNG = INSTRUCBUS[12]; JGRT = INSTRUCBUS[13]; JMP = INSTRUCBUS[14]; JSR = INSTRUCBUS[15];
  //   LD = INSTRUCBUS[16]; ST = INSTRUCBUS[17]; INC = INSTRUCBUS[18]; SUB = INSTRUCBUS[19]; TST = INSTRUCBUS[20];
  //   JADR = INSTRUCBUS[21]; STRCPY = INSTRUCBUS[22]; FETCH = PHASEFFBUS[0]; ADDR = PHASEFFBUS[1];
  //   EXEC = PHASEFFBUS[2]; INTR = PHASEFFBUS[3]; PSWSTART = PSW[0]; PSWZ = PSW[1]; PSWN = PSW[2]; PSWC = PSW[3];
  //   PSWV = PSW[4]; PSWI = PSW[15]; rst = in_1

  // Notes on the sheet:
  //   Akumulator
  //   Operaciona jedinica
  //   Upravljacka jedinica
  //   ALU
  //   AND(TST)
endmodule

module INTR (
  input  in_1,
  input  in_2,
  input  in_3,
  input  [3:0] PHASEFFBUS,
  input  [22:0] INSTRUCBUS,
  input  [15:0] PSW,
  input  [7:0] intr7__0,
  output [15:0] ADDIVTP,
  output [2:0] UEXT2__0,
  output inta,
  output [15:0] CMEMBUS,
  output [7:0] CFFBUS,
  output [31:0] CREGBUS,
  output rdMEM,
  output wrMEM
);

  wire and_2_out, and_3_out, and_4_out, brcnd, brnotFCBUS, brnotINTR, brnotprekid, bruncnd, clINTR, decSP,
       incMAR, ldC7__0, ldC15__8, ldMAR, ldMDR, ldPC, mxMAR0, mxMAR1, mxMAR2, mxMDR0, mxMDR1, mxMDR2, mxMDR3,
       mxPC0, mxPC1, not_1_out, not_2_out, not_3_out, not_4_out, not_5_out, not_6_out, not_7_out, or_1_out,
       prekid, prper, rdMEM_t, stFETCH, wrMEM_t;
  wire [2:0] rom_32x29_1_dout;
  wire [3:1] IVTDSP15__0;
  wire [4:0] reg5_inc_ld_1_a4__0;
  wire [15:0] IVTP15__0;
  wire [28:24] rom_32x29_1_dout_2;

  not not_1 (not_1_out, in_1);
  REG5_INC_LD reg5_inc_ld_1 (
    .I4__0(rom_32x29_1_dout_2), .LD(or_1_out), .INC(not_2_out), .mr(not_1_out), .CLK(in_2),
    .A4__0(reg5_inc_ld_1_a4__0));
  not not_2 (not_2_out, or_1_out);
  DC3_8 dc3_8_1 (
    .X2__0(rom_32x29_1_dout), .D1(bruncnd), .D2(brnotINTR), .D3(brnotprekid), .D4(brnotFCBUS));  // open: En, D0, D5, D6, D7
  and and_1 (prekid, prper, PSW[15], not_3_out);
  not not_3 (not_3_out, INSTRUCBUS[0]);
  or or_1 (or_1_out, bruncnd, brcnd);
  ROM_32x29 rom_32x29_1 (
    .A4__0(reg5_inc_ld_1_a4__0), .CS(1'b1),
    .DOUT({rom_32x29_1_dout_2, rom_32x29_1_dout, clINTR, stFETCH, mxPC1, mxPC0, ldPC, ldC15__8, ldC7__0, incMAR, inta, rdMEM_t, wrMEM_t, decSP, mxMDR3, mxMDR2, mxMDR1, mxMDR0, ldMDR, mxMAR2, mxMAR1, mxMAR0, ldMAR}));
  or or_2 (prper, intr7__0[7], intr7__0[6], intr7__0[5], intr7__0[4], intr7__0[3], intr7__0[2], intr7__0[1], intr7__0[0]);
  not not_4 (not_4_out, in_1);
  // REG16_LD reg16_ld_1: pin names not known; wires that end beside it: in_2, not_4_out, IVTP15__0
  not not_5 (not_5_out, PHASEFFBUS[3]);
  not not_6 (not_6_out, prekid);
  not not_7 (not_7_out, in_3);
  CD8 cd8_1 (
    .En(1'b1), .C7(intr7__0[7]), .C6(intr7__0[6]), .C5(intr7__0[5]), .C4(intr7__0[4]), .C3(intr7__0[3]),
    .C2(intr7__0[2]), .C1(intr7__0[1]), .C0(intr7__0[0]), .Z2(UEXT2__0[2]), .Z1(UEXT2__0[1]), .Z0(UEXT2__0[0]));  // open: W
  and and_2 (and_2_out, not_5_out, brnotINTR);
  and and_3 (and_3_out, not_6_out, brnotprekid);
  and and_4 (and_4_out, not_7_out, brnotFCBUS);
  or or_3 (brcnd, and_2_out, and_3_out, and_4_out);
  REG3_LD reg3_ld_1 (.I2__0(UEXT2__0), .LD(inta), .CLK(in_2), .A2__0(IVTDSP15__0));
  ADD16 add16_1 (.C0(1'b0), .A(IVTP15__0), .B({{12{1'b0}}, IVTDSP15__0, 1'b0}), .F(ADDIVTP));  // open: C16
  assign CMEMBUS[0] = ldMAR ? 1'b1 : 1'bz;  // Controlled_Buffer controlled_buffer_1
  assign CMEMBUS[1] = incMAR ? 1'b1 : 1'bz;  // Controlled_Buffer controlled_buffer_2
  assign CMEMBUS[2] = ldMDR ? 1'b1 : 1'bz;  // Controlled_Buffer controlled_buffer_3
  assign CMEMBUS[3] = ldPC ? 1'b1 : 1'bz;  // Controlled_Buffer controlled_buffer_4
  assign CMEMBUS[5] = mxMAR1 ? 1'b1 : 1'bz;  // Controlled_Buffer controlled_buffer_5
  assign CMEMBUS[6] = mxMAR0 ? 1'b1 : 1'bz;  // Controlled_Buffer controlled_buffer_6
  assign CMEMBUS[8] = decSP ? 1'b1 : 1'bz;  // Controlled_Buffer controlled_buffer_7
  assign CMEMBUS[9] = mxMAR2 ? 1'b1 : 1'bz;  // Controlled_Buffer controlled_buffer_8
  assign CMEMBUS[10] = mxPC1 ? 1'b1 : 1'bz;  // Controlled_Buffer controlled_buffer_9
  assign CMEMBUS[11] = mxPC0 ? 1'b1 : 1'bz;  // Controlled_Buffer controlled_buffer_10
  assign CMEMBUS[12] = mxMDR2 ? 1'b1 : 1'bz;  // Controlled_Buffer controlled_buffer_11
  assign CMEMBUS[13] = mxMDR1 ? 1'b1 : 1'bz;  // Controlled_Buffer controlled_buffer_12
  assign CMEMBUS[14] = mxMDR0 ? 1'b1 : 1'bz;  // Controlled_Buffer controlled_buffer_13
  assign CMEMBUS[15] = mxMDR3 ? 1'b1 : 1'bz;  // Controlled_Buffer controlled_buffer_14
  assign CREGBUS[8] = ldC15__8 ? 1'b1 : 1'bz;  // Controlled_Buffer controlled_buffer_15
  assign CREGBUS[9] = ldC7__0 ? 1'b1 : 1'bz;  // Controlled_Buffer controlled_buffer_16
  assign CFFBUS[0] = stFETCH ? 1'b1 : 1'bz;  // Controlled_Buffer controlled_buffer_17
  assign CFFBUS[7] = clINTR ? 1'b1 : 1'bz;  // Controlled_Buffer controlled_buffer_18
  assign rdMEM = rdMEM_t ? 1'b1 : 1'bz;  // Controlled_Buffer controlled_buffer_19
  assign wrMEM = wrMEM_t ? 1'b1 : 1'bz;  // Controlled_Buffer controlled_buffer_20

  // Other names for the same wires on the sheet: ldBRU = inta; ADDIVTP15__0[15:0] = ADDIVTP; CLK = in_2; FCBUS = in_3;
  //   HALT = INSTRUCBUS[0]; RTS = INSTRUCBUS[1]; RTI = INSTRUCBUS[2]; INTE = INSTRUCBUS[3]; INTD = INSTRUCBUS[4];
  //   PUSH = INSTRUCBUS[5]; POP = INSTRUCBUS[6]; STBR = INSTRUCBUS[7]; STXR = INSTRUCBUS[8]; STAR = INSTRUCBUS[9];
  //   BNEQ = INSTRUCBUS[10]; BOVF = INSTRUCBUS[11]; JNNG = INSTRUCBUS[12]; JGRT = INSTRUCBUS[13];
  //   JMP = INSTRUCBUS[14]; JSR = INSTRUCBUS[15]; LD = INSTRUCBUS[16]; ST = INSTRUCBUS[17]; INC = INSTRUCBUS[18];
  //   SUB = INSTRUCBUS[19]; TST = INSTRUCBUS[20]; JADR = INSTRUCBUS[21]; STRCPY = INSTRUCBUS[22];
  //   INTR = PHASEFFBUS[3]; PSWSTART = PSW[0]; PSWZ = PSW[1]; PSWN = PSW[2]; PSWC = PSW[3]; PSWV = PSW[4];
  //   PSWI = PSW[15]; rst = in_1

  // Notes on the sheet:
  //   Operaciona jedinica
  //   Upravljacka jedinica
endmodule

module RAM (
  input  [15:0] in_1,
  input  in_2,
  input  [7:0] in_3,
  input  in_4,
  input  in_5,
  input  in_6,
  output [7:0] out_7,
  output out_8
);

  wire and_1_out, and_2_out, CNT0, LDCNT, not_1_out, not_2_out, not_3_out, notCNT0, or_1_out, rsff_2_q, sl,
       xor_1_out;
  wire [3:0] CNT, LFSR;

  RSFF rsff_1 (.S(in_6), .CLK(in_2), .R(1'b0), .Q(sl));  // open: Sd, Rd, notQ
  or or_1 (or_1_out, in_4, in_5);
  REG4_LD_SL_SR reg4_ld_sl_sr_1 (
    .I3__0(4'b1111), .LD(in_6), .IR(1'b0), .SR(1'b0), .IL(xor_1_out), .SL(sl), .CLK(in_2), .A3__0(LFSR));
  RisingEdge risingedge_1 (.INPUT(or_1_out), .CLK(in_2), .OUTPUT(LDCNT));
  // MEM64Kx8 mem64kx8_1: pin names not known; wires that end beside it: in_1, 1'b1, in_2, in_3, out_7, in_4
  xor xor_1 (xor_1_out, LFSR[2], LFSR[3]);
  and and_1 (and_1_out, CNT0, not_1_out);
  not not_1 (not_1_out, LDCNT);
  RSFF rsff_2 (.S(LDCNT), .CLK(in_2), .R(and_1_out), .Rd(not_2_out), .Q(rsff_2_q));  // open: Sd, notQ
  not not_2 (not_2_out, in_6);
  and and_2 (and_2_out, rsff_2_q, CNT0);
  REG4m_DEC_LD reg4m_dec_ld_1 (
    .I3__0(LFSR), .LD(LDCNT), .Ein(notCNT0), .DEC(notCNT0), .CLK(in_2), .A3__0(CNT));  // open: Eout
  or or_2 (notCNT0, CNT[0], CNT[1], CNT[2], CNT[3]);
  RSFF rsff_3 (.S(and_2_out), .CLK(in_2), .R(out_8), .Rd(not_3_out), .Q(out_8));  // open: Sd, notQ
  not not_3 (not_3_out, in_6);
  not not_4 (CNT0, notCNT0);

  // Other names for the same wires on the sheet: ADR[15:0] = in_1; CLK = in_2; DIN[7:0] = in_3; DOUT[7:0] = out_7;
  //   fc = out_8; RDMEM = in_5; rst = in_6; WRMEM = in_4

  // Notes on the sheet:
  //   Random broj predstavlja vreme pristupa memoriji
  //   Brojac za generisanje random broja 
  //   Jedinica za generisanje function complete (fc) signala
  //   Brojac za dekrementiranje random broja
endmodule
